# Fritzing sketch SuSoCi-Schema (saved by Fritzing 0.9.4)
breadboards: 1

parts:
  Display1 = LCD screen 16x2 IIC [part_number=101290]
  Bauteil1 = SRF05 Ultrasonic Rangefinder
  Bauteil2 = Arduino Uno (Rev3)

nets:
  GND: Display1.GND, Bauteil1.GND, Bauteil2.GND
  VCC: Display1.VCC, Bauteil1.VCC, Bauteil2.5V
  N1: Display1.SDA, Bauteil2.A4/SDA
  N2: Display1.SCL, Bauteil2.A3
  N3: Bauteil1.Trig, Bauteil2.D13/SCK
  N4: Bauteil1.Echo, Bauteil2.D12/MISO

custom parts:
  LCD screen 16x2 IIC: LCD screen with HD44780 controller enables showing text, symbols, value or anything else that comes from Croduino/Arduino. It is capable of showing 16 symbols in two lines and therefore can be used in many projects that need to send clearly visible and legible output information.. • Color of symbols: White • Backlight: Blue • Dimensions: 80 x 36 x 12 mm • Screen dimensions: 64.5 x 16 mm •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
